// Logisim project Microprocessor.circ as structural Verilog: 2 circuits, main circuit main
module main (
);

  wire undriven, undriven_3, undriven_4, undriven_5, undriven_6, undriven_7, undriven_8, undriven_9,
       undriven_17, undriven_18, undriven_19, undriven_20, undriven_21, undriven_22, undriven_23, undriven_24;
  wire [2:0] undriven_2;
  wire [4:0] main_1_p1;
  wire [6:0] undriven_10;
  wire [7:0] instruction_register_1_output_2;
  wire [8:0] undriven_11, undriven_12, undriven_13, undriven_14, undriven_15;
  wire [10:0] undriven_16;
  wire [15:0] alu_1_ax_4, alu_1_bx_4, alu_1_cx_4, alu_1_dx_4, alu_1_ex_4, general_purpose_1_output,
       general_purpose_2_output, general_purpose_3_output, general_purpose_4_output,
       general_purpose_5_output, instruction_register_1_output, multiplexer_1_out, special_purpose_1_output,
       special_purpose_2_output, special_purpose_3_output;
  wire [23:0] controlled_buffer_1_out, ram_1_data;

  // CONTROL_UNITS_main main_1: pin names not known; wires that end beside it: main_1_p1[0]
  ALU alu_1 (
    .AX_2(main_1_p1[0]), .BX_2(main_1_p1[1]), .CX_2(main_1_p1[2]), .DX_2(main_1_p1[3]), .EX_2(main_1_p1[4]),
    .AX_3(undriven_10[0]), .BX_3(undriven_10[1]), .CX_3(undriven_10[2]), .DX_3(undriven_10[3]),
    .EX_3(undriven_10[4]), .DR_3(undriven_10[5]), .IR_3(undriven_10[6]), .AX(general_purpose_1_output),
    .BX(general_purpose_2_output), .CX(general_purpose_3_output), .DX(general_purpose_4_output),
    .EX(general_purpose_5_output), .DR(special_purpose_3_output), .IR(instruction_register_1_output),
    .AND(undriven_16[10]), .OR(undriven_16[9]), .XOR(undriven_16[8]), .ADD(undriven_16[7]),
    .ADC(undriven_16[6]), .SUB(undriven_16[5]), .SBB(undriven_16[4]), .MUL(undriven_16[3]),
    .DIV(undriven_16[2]), .CMP(undriven_16[1]), .LOAD(undriven_16[0]), .AX_4(alu_1_ax_4), .BX_4(alu_1_bx_4),
    .CX_4(alu_1_cx_4), .DX_4(alu_1_dx_4), .EX_4(alu_1_ex_4));  // open: Cin, DR_2, IR_2, Zero, Cout
  GENERAL_PURPOSE general_purpose_1 (
    .INPUT(alu_1_ax_4), .INC(undriven_11[8]), .LD(undriven_11[7]), .DEC(undriven_11[6]),
    .SHL(undriven_11[5]), .SHR(undriven_11[4]), .CIL(undriven_11[3]), .CIR(undriven_11[2]),
    .CML(undriven_11[1]), .CLR(undriven_11[0]), .OUTPUT(general_purpose_1_output));  // open: CLK
  GENERAL_PURPOSE general_purpose_2 (
    .INPUT(alu_1_bx_4), .INC(undriven_12[8]), .LD(undriven_12[7]), .DEC(undriven_12[6]),
    .SHL(undriven_12[5]), .SHR(undriven_12[4]), .CIL(undriven_12[3]), .CIR(undriven_12[2]),
    .CML(undriven_12[1]), .CLR(undriven_12[0]), .OUTPUT(general_purpose_2_output));  // open: CLK
  GENERAL_PURPOSE general_purpose_3 (
    .INPUT(alu_1_cx_4), .INC(undriven_13[8]), .LD(undriven_13[7]), .DEC(undriven_13[6]),
    .SHL(undriven_13[5]), .SHR(undriven_13[4]), .CIL(undriven_13[3]), .CIR(undriven_13[2]),
    .CML(undriven_13[1]), .CLR(undriven_13[0]), .OUTPUT(general_purpose_3_output));  // open: CLK
  GENERAL_PURPOSE general_purpose_4 (
    .INPUT(alu_1_dx_4), .INC(undriven_14[8]), .LD(undriven_14[7]), .DEC(undriven_14[6]),
    .SHL(undriven_14[5]), .SHR(undriven_14[4]), .CIL(undriven_14[3]), .CIR(undriven_14[2]),
    .CML(undriven_14[1]), .CLR(undriven_14[0]), .OUTPUT(general_purpose_4_output));  // open: CLK
  GENERAL_PURPOSE general_purpose_5 (
    .INPUT(alu_1_ex_4), .INC(undriven_15[8]), .LD(undriven_15[7]), .DEC(undriven_15[6]),
    .SHL(undriven_15[5]), .SHR(undriven_15[4]), .CIL(undriven_15[3]), .CIR(undriven_15[2]),
    .CML(undriven_15[1]), .CLR(undriven_15[0]), .OUTPUT(general_purpose_5_output));  // open: CLK
  Multiplexer #(.select(3), .width(16), .enable("false")) multiplexer_1 (
    .in0(special_purpose_1_output), .in1(general_purpose_1_output), .in2(general_purpose_2_output),
    .in3(general_purpose_3_output), .in4(general_purpose_4_output), .in5(general_purpose_5_output),
    .out(multiplexer_1_out), .sel(undriven_2));  // open: in6, in7
  assign controlled_buffer_1_out = undriven_17 ? {{8{1'b0}}, general_purpose_1_output} : 24'bz;  // Controlled_Buffer controlled_buffer_1
  assign controlled_buffer_1_out = undriven_18 ? {{8{1'b0}}, general_purpose_2_output} : 24'bz;  // Controlled_Buffer controlled_buffer_2
  assign controlled_buffer_1_out = undriven_19 ? {{8{1'b0}}, general_purpose_3_output} : 24'bz;  // Controlled_Buffer controlled_buffer_3
  assign controlled_buffer_1_out = undriven_20 ? {{8{1'b0}}, general_purpose_4_output} : 24'bz;  // Controlled_Buffer controlled_buffer_4
  assign controlled_buffer_1_out = undriven_3 ? {{8{1'b0}}, general_purpose_5_output} : 24'bz;  // Controlled_Buffer controlled_buffer_5
  SPECIAL_PURPOSE special_purpose_1 (
    .INPUT(controlled_buffer_1_out[15:0]), .LD(undriven_8), .OUTPUT(special_purpose_1_output));  // open: INC, CLK
  SPECIAL_PURPOSE special_purpose_2 (
    .INPUT(controlled_buffer_1_out[15:0]), .INC(undriven_21), .LD(undriven_5),
    .OUTPUT(special_purpose_2_output));  // open: CLK
  SPECIAL_PURPOSE special_purpose_3 (
    .INPUT(controlled_buffer_1_out[15:0]), .LD(undriven_22), .OUTPUT(special_purpose_3_output));  // open: INC, CLK
  INSTRUCTION_REGISTER instruction_register_1 (
    .INPUT(controlled_buffer_1_out), .LOAD(undriven_7),
    .OUTPUT({instruction_register_1_output_2, instruction_register_1_output}));
  RAM #(.addrWidth(16), .dataWidth(24), .bus("separate")) ram_1 (
    .addr(multiplexer_1_out), .din(controlled_buffer_1_out), .data(ram_1_data), .str(undriven_23));  // open: sel, clk, ld, clr
  assign controlled_buffer_1_out = undriven_9 ? {{8{1'b0}}, special_purpose_1_output} : 24'bz;  // Controlled_Buffer controlled_buffer_6
  assign controlled_buffer_1_out = undriven_4 ? {{8{1'b0}}, special_purpose_2_output} : 24'bz;  // Controlled_Buffer controlled_buffer_7
  assign controlled_buffer_1_out = undriven_24 ? {{8{1'b0}}, special_purpose_3_output} : 24'bz;  // Controlled_Buffer controlled_buffer_8
  assign controlled_buffer_1_out = undriven_6 ? {instruction_register_1_output_2, instruction_register_1_output} : 24'bz;  // Controlled_Buffer controlled_buffer_9
  assign controlled_buffer_1_out = undriven ? ram_1_data : 24'bz;  // Controlled_Buffer controlled_buffer_10

  // Notes on the sheet:
  //   AR
  //   PC
  //   DR
  //   IR
endmodule

module FLAG (
  input  CLK,
  input  INPUT,
  input  CLR,
  input  CML
);

  Multiplexer #(.select(3)) multiplexer_1 ();  // open: in0, in1, in2, in3, in4, in5, in6, in7, out, sel, en
  D_Flip_Flop d_ff_1 ();  // open: clk, D, Q, Qn, preset, en, reset
endmodule
